// Logisim project ULA.circ as structural Verilog: 1 circuit, main circuit main
module main (
  input  in_1,
  input  in_2,
  input  in_3,
  input  in_4,
  input  in_5,
  input  in_6,
  input  in_7,
  input  in_8,
  input  in_9,
  input  in_10,
  input  in_11,
  input  in_12,
  input  in_13,
  input  in_14,
  input  in_15,
  input  in_16,
  input  in_17,
  input  in_18,
  input  in_19,
  input  in_20,
  input  in_21,
  input  in_22
);

  wire A0_out, A1_out, A2_out, A3_out, A4_out, A5_out, A6_out, A7_out, and_5_out, and_6_out, and_7_out,
       and_8_out, and_9_out, and_10_out, and_11_out, and_12_out, and_13_out, and_14_out, and_15_out,
       and_16_out, and_17_out, and_18_out, and_19_out, and_20_out, and_21_out, and_22_out, and_23_out,
       and_24_out, and_25_out, and_26_out, and_27_out, and_28_out, and_29_out, and_30_out, and_31_out,
       and_32_out, and_33_out, and_34_out, and_35_out, and_36_out, not_1_out, not_2_out, not_3_out,
       not_4_out, not_5_out, not_6_out, not_7_out, not_8_out, not_9_out, not_10_out, not_11_out, not_12_out,
       not_13_out, not_14_out, not_15_out, not_16_out, not_17_out, not_18_out, not_19_out, or_5_out,
       or_6_out, or_7_out, or_8_out, or_9_out, undriven, undriven_2, undriven_3, undriven_4, undriven_5,
       undriven_6, undriven_7, undriven_8, undriven_9, undriven_10, undriven_11, undriven_12, undriven_13,
       undriven_14, undriven_15, undriven_16, undriven_17, undriven_18, undriven_19, undriven_20,
       undriven_21, undriven_22, undriven_23, undriven_24, undriven_25, undriven_26, undriven_27,
       undriven_28, undriven_29, undriven_30, undriven_31, undriven_32;

  // AND_Gate and_1 has open pins: in0=in_4, in1=in_8, out=open
  // AND_Gate and_2 has open pins: in0=in_3, in1=in_7, out=open
  // AND_Gate and_3 has open pins: in0=in_2, in1=in_6, out=open
  // AND_Gate and_4 has open pins: in0=in_1, in1=in_5, out=open
  // OR_Gate or_1 has open pins: in0=in_4, in1=in_8, out=open
  // OR_Gate or_2 has open pins: in0=in_3, in1=in_7, out=open
  // OR_Gate or_3 has open pins: in0=in_2, in1=in_6, out=open
  // OR_Gate or_4 has open pins: in0=in_1, in1=in_5, out=open
  // XOR_Gate xor_1 has open pins: in0=in_4, in1=in_8, out=open
  // XOR_Gate xor_2 has open pins: in0=in_3, in1=in_7, out=open
  // XOR_Gate xor_3 has open pins: in0=in_2, in1=in_6, out=open
  // XOR_Gate xor_4 has open pins: in0=in_1, in1=in_5, out=open
  not not_1 (not_1_out, in_8);
  not not_2 (not_2_out, in_7);
  not not_3 (not_3_out, in_6);
  not not_4 (not_4_out, in_5);
  not not_5 (not_5_out, in_9);
  not not_6 (not_6_out, in_10);
  not not_7 (not_7_out, in_9);
  not not_8 (not_8_out, in_10);
  not not_9 (not_9_out, in_9);
  not not_10 (not_10_out, in_10);
  not not_11 (not_11_out, in_9);
  not not_12 (not_12_out, in_10);
  not not_13 (not_13_out, in_11);
  not not_14 (not_14_out, in_11);
  not not_15 (not_15_out, in_11);
  not not_16 (not_16_out, in_11);
  and and_5 (and_5_out, undriven, not_13_out, not_6_out, not_5_out);
  and and_6 (and_6_out, undriven_3, not_13_out, in_10, not_5_out);
  and and_7 (and_7_out, undriven_5, not_13_out, not_6_out, in_9);
  and and_8 (and_8_out, undriven_7, not_13_out, in_10, in_9);
  and and_9 (and_9_out, undriven_9, not_14_out, not_8_out, not_7_out);
  and and_10 (and_10_out, undriven_11, not_14_out, in_10, not_7_out);
  and and_11 (and_11_out, undriven_13, not_14_out, not_8_out, in_9);
  and and_12 (and_12_out, undriven_15, not_14_out, in_10, in_9);
  and and_13 (and_13_out, undriven_17, not_15_out, not_10_out, not_9_out);
  and and_14 (and_14_out, undriven_19, not_15_out, in_10, not_9_out);
  and and_15 (and_15_out, undriven_21, not_15_out, not_10_out, in_9);
  and and_16 (and_16_out, undriven_23, not_15_out, in_10, in_9);
  and and_17 (and_17_out, undriven_25, not_16_out, not_12_out, not_11_out);
  and and_18 (and_18_out, undriven_27, not_16_out, in_10, not_11_out);
  and and_19 (and_19_out, undriven_29, not_16_out, not_12_out, in_9);
  and and_20 (and_20_out, undriven_31, not_16_out, in_10, in_9);
  and and_21 (and_21_out, undriven_2, in_11, not_6_out, not_5_out);
  and and_22 (and_22_out, undriven_4, in_11, in_10, not_5_out);
  and and_23 (and_23_out, undriven_6, in_11, not_6_out, in_9);
  and and_24 (and_24_out, undriven_8, in_11, in_10, in_9);
  and and_25 (and_25_out, undriven_10, in_11, not_8_out, not_7_out);
  and and_26 (and_26_out, undriven_12, in_11, in_10, not_7_out);
  and and_27 (and_27_out, undriven_14, in_11, not_8_out, in_9);
  and and_28 (and_28_out, undriven_16, in_11, in_10, in_9);
  and and_29 (and_29_out, undriven_18, in_11, not_10_out, not_9_out);
  and and_30 (and_30_out, undriven_20, in_11, in_10, not_9_out);
  and and_31 (and_31_out, undriven_22, in_11, not_10_out, in_9);
  and and_32 (and_32_out, undriven_24, in_11, in_10, in_9);
  and and_33 (and_33_out, undriven_26, in_11, not_12_out, not_11_out);
  and and_34 (and_34_out, undriven_28, in_11, in_10, not_11_out);
  and and_35 (and_35_out, undriven_30, in_11, not_12_out, in_9);
  and and_36 (and_36_out, undriven_32, in_11, in_10, in_9);
  or or_5 (or_5_out, and_5_out, and_21_out, and_6_out, and_22_out, and_7_out, and_23_out, and_8_out, and_24_out);
  or or_6 (or_6_out, and_9_out, and_25_out, and_10_out, and_26_out, and_11_out, and_27_out, and_12_out, and_28_out);
  or or_7 (or_7_out, and_13_out, and_29_out, and_14_out, and_30_out, and_15_out, and_31_out, and_16_out, and_32_out);
  or or_8 (or_8_out, and_17_out, and_33_out, and_18_out, and_34_out, and_19_out, and_35_out, and_20_out, and_36_out);
  LED led_1 ();  // open: in
  LED led_2 ();  // open: in
  LED led_3 ();  // open: in
  LED led_4 ();  // open: in
  not not_17 (not_17_out, in_12);
  not not_18 (not_18_out, in_13);
  not not_19 (not_19_out, in_14);
  LED led_5 (.in(or_9_out));
  and A0 (A0_out, in_15, not_19_out, not_18_out, not_17_out);
  and A2 (A2_out, in_17, not_19_out, in_13, not_17_out);
  and A4 (A4_out, in_19, not_19_out, not_18_out, in_12);
  and A6 (A6_out, in_21, not_19_out, in_13, in_12);
  and A1 (A1_out, in_16, in_14, not_18_out, not_17_out);
  and A3 (A3_out, in_18, in_14, in_13, not_17_out);
  and A5 (A5_out, in_20, in_14, not_18_out, in_12);
  and A7 (A7_out, in_22, in_14, in_13, in_12);
  or or_9 (or_9_out, A0_out, A1_out, A2_out, A3_out, A4_out, A5_out, A6_out, A7_out);

  // Notes on the sheet:
  //   8x1 MUX
endmodule
